// Digital circuit Calculador-Paridade.dig as structural Verilog
module Calculador_Paridade (
  input  D0,
  input  D1,
  input  D2,
  input  D3,
  input  P,
  output LED
);

  wire xor_2_out;

  xor xor_1 (LED, xor_2_out, P);
  xor xor_2 (xor_2_out, D0, D1, D2, D3);

  // Notes on the sheet:
  //   D0: D0
  //   D1: D1
  //   D2: D2
  //   D3: D3
  //   P: P
  //   LED: LED
endmodule
