// Digital circuit Ex1.dig as structural Verilog
module Ex1 (
  input  P,
  input  D3,
  input  D2,
  input  D1,
  input  D0,
  input  SHIFT,
  input  RESET,
  input  clk,
  input  _1,
  output D3_2,
  output D2_2,
  output D1_2,
  output D0_2,
  output P_2
);

  wire calculador_paridade_1_led, driver_1_out, parallel_in___serial_out_1_serial;

  assign driver_1_out = SHIFT ? clk : 1'bz;  // Driver driver_1
  Serial_in___parallel_out serial_in___parallel_out_1 (
    .ENTRADA(parallel_in___serial_out_1_serial), .CLOCK(driver_1_out), .RESET(RESET), .D0(D0_2), .D1(D1_2),
    .D2(D2_2), .D3(D3_2), .P(P_2));
  Parallel_in___serial_out parallel_in___serial_out_1 (
    .SHIFT_LOAD(SHIFT), .CLOCK(clk), ._1(_1), ._0(1'b0), .D0(D0), .D1(D1), .D2(D2), .D3(D3), .P(P),
    .SERIAL(parallel_in___serial_out_1_serial));
  Calculador_Paridade calculador_paridade_1 (
    .D0(D0_2), .D1(D1_2), .D2(D2_2), .D3(D3_2), .P(P_2), .LED(calculador_paridade_1_led));
  LED led_1 (.in(calculador_paridade_1_led));

  // Notes on the sheet:
  //   P: P
  //   D3: D3
  //   D2: D2
  //   D1: D1
  //   D0: D0
  //   SHIFT: SHIFT
  //   RESET: RESET
  //   P_2: P
  //   clk: Hz: 10
  //   _1: 1
endmodule
