// Digital circuit Parallel in - serial out.dig as structural Verilog
module Parallel_in___serial_out (
  input  SHIFT_LOAD,
  input  CLOCK,
  input  _1,
  input  _0,
  input  D0,
  input  D1,
  input  D2,
  input  D3,
  input  P,
  output SERIAL
);

  wire and_1_out, and_2_out, and_3_out, and_4_out, and_5_out, and_6_out, and_7_out, and_8_out, and_9_out,
       and_10_out, and_11_out, and_12_out, and_13_out, d_ff_1_q, d_ff_2_q, d_ff_3_q, d_ff_4_q, d_ff_5_q,
       d_ff_6_q, d_ff_7_q, not_1_out, or_1_out, or_2_out, or_3_out, or_4_out, or_5_out, or_6_out;

  not not_1 (not_1_out, SHIFT_LOAD);
  and and_1 (and_1_out, P, not_1_out);
  D_FF d_ff_1 (.D(and_1_out), .C(CLOCK), .Q(d_ff_1_q));  // open: nQ
  and and_2 (and_2_out, SHIFT_LOAD, d_ff_1_q);
  or or_1 (or_1_out, and_3_out, and_2_out);
  D_FF d_ff_2 (.D(or_1_out), .C(CLOCK), .Q(d_ff_2_q));  // open: nQ
  and and_3 (and_3_out, D3, not_1_out);
  and and_4 (and_4_out, SHIFT_LOAD, d_ff_2_q);
  D_FF d_ff_3 (.D(or_2_out), .C(CLOCK), .Q(d_ff_3_q));  // open: nQ
  and and_5 (and_5_out, D2, not_1_out);
  or or_2 (or_2_out, and_5_out, and_4_out);
  and and_6 (and_6_out, SHIFT_LOAD, d_ff_3_q);
  or or_3 (or_3_out, and_7_out, and_6_out);
  D_FF d_ff_4 (.D(or_3_out), .C(CLOCK), .Q(d_ff_4_q));  // open: nQ
  and and_7 (and_7_out, D1, not_1_out);
  and and_8 (and_8_out, SHIFT_LOAD, d_ff_4_q);
  and and_9 (and_9_out, D0, not_1_out);
  or or_4 (or_4_out, and_9_out, and_8_out);
  D_FF d_ff_5 (.D(or_4_out), .C(CLOCK), .Q(d_ff_5_q));  // open: nQ
  and and_10 (and_10_out, SHIFT_LOAD, d_ff_5_q);
  or or_5 (or_5_out, and_11_out, and_10_out);
  D_FF d_ff_6 (.D(or_5_out), .C(CLOCK), .Q(d_ff_6_q));  // open: nQ
  and and_11 (and_11_out, _0, not_1_out);
  and and_12 (and_12_out, SHIFT_LOAD, d_ff_6_q);
  and and_13 (and_13_out, _1, not_1_out);
  or or_6 (or_6_out, and_13_out, and_12_out);
  D_FF d_ff_7 (.D(or_6_out), .C(CLOCK), .Q(d_ff_7_q));  // open: nQ
  assign SERIAL = SHIFT_LOAD ? d_ff_7_q : 1'bz;  // Driver driver_1

  // Notes on the sheet:
  //   SHIFT_LOAD: SHIFT/LOAD
  //   CLOCK: CLOCK
  //   _1: 1
  //   _0: 10
  //   D0: D0
  //   D1: D1
  //   D2: D2
  //   D3: D3
  //   SERIAL: SERIAL
  //   P: P
endmodule
