// Digital circuit Registrador-4bits-DLATCH.dig as structural Verilog
module Registrador_4bits_DLATCH (
  input  WE,
  input  d3_2,
  input  d2_2,
  input  d1_2,
  input  d0_2,
  output D3,
  output D2,
  output D1,
  output D0
);

  D_FF d_ff_1 (.D(d3_2), .C(WE), .Q(D3));  // open: nQ
  D_FF d_ff_2 (.D(d2_2), .C(WE), .Q(D2));  // open: nQ
  D_FF d_ff_3 (.D(d1_2), .C(WE), .Q(D1));  // open: nQ
  D_FF d_ff_4 (.D(d0_2), .C(WE), .Q(D0));  // open: nQ

  // Notes on the sheet:
  //   WE: WE
  //   D3: D3
  //   D2: D2
  //   D1: D1
  //   D0: D0
  //   d3_2: d3
  //   d2_2: d2
  //   d1_2: d1
  //   d0_2: d0
endmodule
