// Digital circuit Serial in - parallel out.dig as structural Verilog
module Serial_in___parallel_out (
  input  ENTRADA,
  input  CLOCK,
  input  RESET,
  output D0,
  output D1,
  output D2,
  output D3,
  output P
);

  wire d_ff_as_1_q, d_ff_as_3_q, d_ff_as_4_q, d_ff_as_7_q, d_ff_as_9_q, d_ff_as_11_q, d_ff_as_12_q,
       jk_ff_as_1_q;

  D_FF_AS d_ff_as_1 (.Set(1'b0), .D(ENTRADA), .C(CLOCK), .Clr(RESET), .Q(d_ff_as_1_q));  // open: nQ
  D_FF_AS d_ff_as_2 (.Set(1'b0), .D(d_ff_as_1_q), .C(jk_ff_as_1_q), .Clr(RESET), .Q(P));  // open: nQ
  D_FF_AS d_ff_as_3 (.Set(1'b0), .D(d_ff_as_1_q), .C(CLOCK), .Clr(RESET), .Q(d_ff_as_3_q));  // open: nQ
  D_FF_AS d_ff_as_4 (.Set(1'b0), .D(d_ff_as_3_q), .C(CLOCK), .Clr(RESET), .Q(d_ff_as_4_q));  // open: nQ
  D_FF_AS d_ff_as_5 (.Set(1'b0), .D(d_ff_as_3_q), .C(jk_ff_as_1_q), .Clr(RESET), .Q(D3));  // open: nQ
  D_FF_AS d_ff_as_6 (.Set(1'b0), .D(d_ff_as_4_q), .C(jk_ff_as_1_q), .Clr(RESET), .Q(D2));  // open: nQ
  D_FF_AS d_ff_as_7 (.Set(1'b0), .D(d_ff_as_4_q), .C(CLOCK), .Clr(RESET), .Q(d_ff_as_7_q));  // open: nQ
  D_FF_AS d_ff_as_8 (.Set(1'b0), .D(d_ff_as_7_q), .C(jk_ff_as_1_q), .Clr(RESET), .Q(D1));  // open: nQ
  D_FF_AS d_ff_as_9 (.Set(1'b0), .D(d_ff_as_7_q), .C(CLOCK), .Clr(RESET), .Q(d_ff_as_9_q));  // open: nQ
  D_FF_AS d_ff_as_10 (.Set(1'b0), .D(d_ff_as_9_q), .C(jk_ff_as_1_q), .Clr(RESET), .Q(D0));  // open: nQ
  D_FF_AS d_ff_as_11 (.Set(1'b0), .D(d_ff_as_9_q), .C(CLOCK), .Clr(RESET), .Q(d_ff_as_11_q));  // open: nQ
  D_FF_AS d_ff_as_12 (.Set(1'b0), .D(d_ff_as_11_q), .C(CLOCK), .Clr(RESET), .Q(d_ff_as_12_q));  // open: nQ
  JK_FF_AS jk_ff_as_1 (.Set(1'b0), .J(1'b1), .C(d_ff_as_12_q), .K(1'b0), .Clr(RESET), .Q(jk_ff_as_1_q));  // open: nQ

  // Notes on the sheet:
  //   ENTRADA: ENTRADA
  //   CLOCK: CLOCK
  //   RESET: RESET
  //   D0: D0
  //   D1: D1
  //   D2: D2
  //   D3: D3
  //   P: P
endmodule
