// Digital circuit TESTE.dig as structural Verilog
module TESTE (
  input  SHIFT_LOAD,
  input  _1,
  input  _0,
  input  D0,
  input  D1,
  input  D2,
  input  D3,
  input  P,
  input  clk,
  input  RESET,
  output D0_2,
  output D1_2,
  output D2_2,
  output D3_2,
  output P_2
);

  wire and_1_out, and_2_out, and_3_out, and_4_out, and_5_out, and_6_out, and_7_out, and_8_out, and_9_out,
       and_10_out, and_11_out, and_12_out, and_13_out, d_ff_1_q, d_ff_2_q, d_ff_3_q, d_ff_4_q, d_ff_5_q,
       d_ff_6_q, d_ff_7_q, d_ff_8_q, d_ff_9_q, d_ff_10_q, d_ff_11_q, d_ff_12_q, d_ff_13_q, d_ff_14_q,
       driver_1_out, driver_2_out, jk_ff_as_1_q, not_1_out, or_1_out, or_2_out, or_3_out, or_4_out, or_5_out,
       or_6_out;

  not not_1 (not_1_out, SHIFT_LOAD);
  and and_1 (and_1_out, P, not_1_out);
  D_FF d_ff_1 (.D(and_1_out), .C(clk), .Q(d_ff_1_q));  // open: nQ
  assign driver_1_out = SHIFT_LOAD ? clk : 1'bz;  // Driver driver_1
  and and_2 (and_2_out, SHIFT_LOAD, d_ff_1_q);
  or or_1 (or_1_out, and_3_out, and_2_out);
  D_FF d_ff_2 (.D(or_1_out), .C(clk), .Q(d_ff_2_q));  // open: nQ
  and and_3 (and_3_out, D3, not_1_out);
  and and_4 (and_4_out, SHIFT_LOAD, d_ff_2_q);
  and and_5 (and_5_out, D2, not_1_out);
  or or_2 (or_2_out, and_5_out, and_4_out);
  D_FF d_ff_3 (.D(or_2_out), .C(clk), .Q(d_ff_3_q));  // open: nQ
  and and_6 (and_6_out, SHIFT_LOAD, d_ff_3_q);
  or or_3 (or_3_out, and_7_out, and_6_out);
  D_FF d_ff_4 (.D(or_3_out), .C(clk), .Q(d_ff_4_q));  // open: nQ
  and and_7 (and_7_out, D1, not_1_out);
  and and_8 (and_8_out, SHIFT_LOAD, d_ff_4_q);
  or or_4 (or_4_out, and_9_out, and_8_out);
  D_FF d_ff_5 (.D(or_4_out), .C(clk), .Q(d_ff_5_q));  // open: nQ
  and and_9 (and_9_out, D0, not_1_out);
  and and_10 (and_10_out, SHIFT_LOAD, d_ff_5_q);
  and and_11 (and_11_out, _0, not_1_out);
  or or_5 (or_5_out, and_11_out, and_10_out);
  D_FF d_ff_6 (.D(or_5_out), .C(clk), .Q(d_ff_6_q));  // open: nQ
  and and_12 (and_12_out, SHIFT_LOAD, d_ff_6_q);
  or or_6 (or_6_out, and_13_out, and_12_out);
  D_FF d_ff_7 (.D(or_6_out), .C(clk), .Q(d_ff_7_q));  // open: nQ
  and and_13 (and_13_out, _1, not_1_out);
  D_FF d_ff_8 (.D(driver_2_out), .C(driver_1_out), .Q(d_ff_8_q));  // open: nQ
  assign driver_2_out = SHIFT_LOAD ? d_ff_7_q : 1'bz;  // Driver driver_2
  D_FF d_ff_9 (.D(d_ff_8_q), .C(driver_1_out), .Q(d_ff_9_q));  // open: nQ
  D_FF_AS d_ff_as_1 (.Set(1'b0), .D(d_ff_8_q), .C(jk_ff_as_1_q), .Clr(RESET), .Q(P_2));  // open: nQ
  D_FF d_ff_10 (.D(d_ff_9_q), .C(driver_1_out), .Q(d_ff_10_q));  // open: nQ
  D_FF_AS d_ff_as_2 (.Set(1'b0), .D(d_ff_9_q), .C(jk_ff_as_1_q), .Clr(RESET), .Q(D3_2));  // open: nQ
  D_FF d_ff_11 (.D(d_ff_10_q), .C(driver_1_out), .Q(d_ff_11_q));  // open: nQ
  D_FF_AS d_ff_as_3 (.Set(1'b0), .D(d_ff_10_q), .C(jk_ff_as_1_q), .Clr(RESET), .Q(D2_2));  // open: nQ
  D_FF d_ff_12 (.D(d_ff_11_q), .C(driver_1_out), .Q(d_ff_12_q));  // open: nQ
  D_FF_AS d_ff_as_4 (.Set(1'b0), .D(d_ff_11_q), .C(jk_ff_as_1_q), .Clr(RESET), .Q(D1_2));  // open: nQ
  D_FF d_ff_13 (.D(d_ff_12_q), .C(driver_1_out), .Q(d_ff_13_q));  // open: nQ
  D_FF_AS d_ff_as_5 (.Set(1'b0), .D(d_ff_12_q), .C(jk_ff_as_1_q), .Clr(RESET), .Q(D0_2));  // open: nQ
  D_FF d_ff_14 (.D(d_ff_13_q), .C(driver_1_out), .Q(d_ff_14_q));  // open: nQ
  JK_FF_AS jk_ff_as_1 (.Set(1'b0), .J(1'b1), .C(d_ff_14_q), .K(1'b0), .Clr(RESET), .Q(jk_ff_as_1_q));  // open: nQ

  // Notes on the sheet:
  //   SHIFT_LOAD: SHIFT/LOAD
  //   _1: 1
  //   _0: 10
  //   D0: D0
  //   D1: D1
  //   D2: D2
  //   D3: D3
  //   P: P
  //   RESET: RESET
  //   D0_2: D0
  //   D1_2: D1
  //   D2_2: D2
  //   D3_2: D3
  //   P_2: P
endmodule
