// Digital circuit Contador.dig as structural Verilog
module Contador (
  input  CLOCK,
  input  RESET,
  output Q3,
  output Q2,
  output Q1,
  output Q0
);

  wire d_ff_as_1_nq, d_ff_as_2_nq, d_ff_as_3_nq, d_ff_as_4_nq;

  D_FF_AS d_ff_as_1 (.Set(1'b0), .D(d_ff_as_1_nq), .C(CLOCK), .Clr(RESET), .Q(Q0), .nQ(d_ff_as_1_nq));
  D_FF_AS d_ff_as_2 (.Set(1'b0), .D(d_ff_as_2_nq), .C(d_ff_as_1_nq), .Clr(RESET), .Q(Q1), .nQ(d_ff_as_2_nq));
  D_FF_AS d_ff_as_3 (.Set(1'b0), .D(d_ff_as_3_nq), .C(d_ff_as_2_nq), .Clr(RESET), .Q(Q2), .nQ(d_ff_as_3_nq));
  D_FF_AS d_ff_as_4 (.Set(1'b0), .D(d_ff_as_4_nq), .C(d_ff_as_3_nq), .Clr(RESET), .Q(Q3), .nQ(d_ff_as_4_nq));

  // Notes on the sheet:
  //   CLOCK: CLOCK
  //   Q3: Q3
  //   Q2: Q2
  //   Q1: Q1
  //   Q0: Q0
  //   RESET: RESET
endmodule
