// Digital circuit EX2.dig as structural Verilog
module EX2 (
  input  RESET,
  input  CLOCK,
  output _1155,
  output _15,
  output _11,
  output _7
);

  wire contador_1_q0, contador_1_q1, contador_1_q2, contador_1_q3, contador_2_q0, contador_2_q1,
       contador_2_q3, contador_3_q0, contador_3_q1, contador_3_q2, contador_4_q1, or_1_out, or_2_out,
       or_3_out, or_4_out;

  or or_1 (or_1_out, RESET, _15);
  Contador contador_1 (
    .CLOCK(CLOCK), .RESET(or_1_out), .Q3(contador_1_q3), .Q2(contador_1_q2), .Q1(contador_1_q1),
    .Q0(contador_1_q0));
  and and_1 (_15, contador_1_q3, contador_1_q2, contador_1_q1, contador_1_q0);
  or or_2 (or_2_out, RESET, _11);
  Contador contador_2 (
    .CLOCK(_15), .RESET(or_2_out), .Q3(contador_2_q3), .Q1(contador_2_q1), .Q0(contador_2_q0));  // open: Q2
  and and_2 (_11, contador_2_q3, contador_2_q1, contador_2_q0);
  Contador contador_3 (
    .CLOCK(_11), .RESET(or_3_out), .Q2(contador_3_q2), .Q1(contador_3_q1), .Q0(contador_3_q0));  // open: Q3
  or or_3 (or_3_out, RESET, _7);
  and and_3 (_7, contador_3_q2, contador_3_q1, contador_3_q0);
  or or_4 (or_4_out, RESET, contador_4_q1);
  Contador contador_4 (.CLOCK(_7), .RESET(or_4_out), .Q1(contador_4_q1), .Q0(_1155));  // open: Q3, Q2

  // Notes on the sheet:
  //   RESET: RESET, default 1
  //   CLOCK: Hz: 5
  //   _1155: /155
  //   _15: /15
  //   _11: /11
  //   _7: /7
endmodule
