// Digital circuit ex3.dig as structural Verilog
module ex3 (
  input  CLOCK,
  input  F,
  output A,
  output B,
  output C,
  output D
);

  wire and_1_out, and_2_out, xor_1_out, xor_2_out, xor_3_out;

  and and_1 (and_1_out, xor_1_out, and_2_out);
  JK_FF jk_ff_1 (.J(and_1_out), .C(CLOCK), .K(and_1_out), .Q(D));  // open: nQ
  xor xor_1 (xor_1_out, F, C);
  JK_FF jk_ff_2 (.J(and_2_out), .C(CLOCK), .K(and_2_out), .Q(C));  // open: nQ
  and and_2 (and_2_out, xor_2_out, xor_3_out);
  xor xor_2 (xor_2_out, F, B);
  JK_FF jk_ff_3 (.J(xor_3_out), .C(CLOCK), .K(xor_3_out), .Q(B));  // open: nQ
  xor xor_3 (xor_3_out, F, A);
  JK_FF jk_ff_4 (.J(1'b1), .C(CLOCK), .K(1'b1), .Q(A));  // open: nQ

  // Notes on the sheet:
  //   CLOCK: CLOCK
  //   F: F
  //   A: A
  //   B: B
  //   C: C
  //   D: D
endmodule
