// Digital circuit ex4.dig as structural Verilog
module ex4 (
  input  CLOCK,
  output C,
  output B,
  output A,
  output Cn,
  output Bn,
  output An
);

  wire and_1_out, and_2_out, and_3_out, and_4_out, and_5_out, and_6_out, or_1_out, or_2_out, or_3_out;

  and and_1 (and_1_out, Bn, C);
  or or_1 (or_1_out, and_3_out, and_2_out, and_1_out);
  D_FF d_ff_1 (.D(or_1_out), .C(CLOCK), .Q(C), .nQ(Cn));
  and and_2 (and_2_out, An, C);
  and and_3 (and_3_out, A, B, Cn);
  and and_4 (and_4_out, A, Bn);
  or or_2 (or_2_out, and_5_out, and_4_out);
  D_FF d_ff_2 (.D(or_2_out), .C(CLOCK), .Q(B), .nQ(Bn));
  and and_5 (and_5_out, An, B);
  or or_3 (or_3_out, and_6_out, An);
  D_FF d_ff_3 (.D(or_3_out), .C(CLOCK), .Q(A), .nQ(An));
  and and_6 (and_6_out, B, C);

  // Notes on the sheet:
  //   CLOCK: CLOCK
  //   C: C
  //   B: B
  //   A: A
  //   Cn: C~
  //   Bn: B~
  //   An: A~
endmodule
